// Logisim project ukol1.circ as structural Verilog: 1 circuit, main circuit main
module main (
  input  in_1
);

  wire and_1_out, and_2_out, and_3_out, and_4_out, and_5_out, and_6_out, clock_1_out, not_1_out, not_2_out,
       or_1_out, or_2_out, t_ff_1_q, t_ff_2_q, t_ff_3_q;

  LED led_1 (.in(t_ff_2_q));
  LED led_2 (.in(t_ff_1_q));
  not not_1 (not_1_out, t_ff_3_q);
  LED led_3 (.in(t_ff_3_q));
  not not_2 (not_2_out, in_1);
  and and_1 (and_1_out, t_ff_1_q, not_2_out);
  and and_2 (and_2_out, t_ff_2_q, t_ff_3_q, not_2_out);
  and and_3 (and_3_out, in_1, t_ff_2_q, not_1_out);
  and and_4 (and_4_out, t_ff_1_q, not_2_out);
  and and_5 (and_5_out, t_ff_3_q, t_ff_2_q);
  and and_6 (and_6_out, t_ff_2_q, in_1);
  or or_1 (or_1_out, and_1_out, and_3_out, and_2_out);
  or or_2 (or_2_out, and_4_out, and_6_out, and_5_out);
  Clock clock_1 (.out(clock_1_out));
  T_Flip_Flop t_ff_1 (.clk(clock_1_out), .T(t_ff_1_q), .Q(t_ff_1_q));  // open: Qn, preset, reset, en
  T_Flip_Flop t_ff_2 (.clk(clock_1_out), .T(or_1_out), .Q(t_ff_2_q));  // open: Qn, preset, reset, en
  T_Flip_Flop t_ff_3 (.clk(clock_1_out), .T(or_2_out), .Q(t_ff_3_q));  // open: Qn, preset, reset, en

  // Notes on the sheet:
  //   q1
  //   q2
  //   q0
endmodule
